// Logisim project breadboard_computer_simulation.circ as structural Verilog: 9 circuits, main circuit CD74HC173_quad_D_type_flip_flop
module main (
  input  in_1,
  input  [7:0] in_2
);

  wire bus0, bus1, bus2, bus3, bus4, bus5, bus6, bus7;

  LED led_1 (.in(bus6));
  LED led_2 (.in(bus5));
  LED led_3 (.in(bus4));
  LED led_4 (.in(bus7));
  LED led_5 (.in(bus3));
  LED led_6 (.in(bus2));
  LED led_7 (.in(bus1));
  LED led_8 (.in(bus0));
  SN74HC245_octal_bus_transceiver_up sn74hc245_octal_bus_transceiver_up_1 (
    .B1(bus7), .B2(bus6), .B3(bus5), .B4(bus4), .B5(bus3), .B6(bus2), .B7(bus1), .B8(bus0),
    .OE_active_low(in_1), .A1(in_2[7]), .A2(in_2[6]), .A3(in_2[5]), .A4(in_2[4]), .A5(in_2[3]), .DIR(1'b1),
    .A6(in_2[2]), .A7(in_2[1]), .A8(in_2[0]));

  // Notes on the sheet:
  //   SYSTEM BUS
endmodule

module system_bus (
  input  in_1,
  input  [7:0] in_2
);

  wire bus0, bus1, bus2, bus3, bus4, bus5, bus6, bus7;

  LED led_1 (.in(bus6));
  LED led_2 (.in(bus5));
  LED led_3 (.in(bus4));
  LED led_4 (.in(bus7));
  LED led_5 (.in(bus3));
  LED led_6 (.in(bus2));
  LED led_7 (.in(bus1));
  LED led_8 (.in(bus0));
  SN74HC245_octal_bus_transceiver_up sn74hc245_octal_bus_transceiver_up_1 (
    .B1(bus7), .B2(bus6), .B3(bus5), .B4(bus4), .B5(bus3), .B6(bus2), .B7(bus1), .B8(bus0),
    .OE_active_low(in_1), .A1(in_2[7]), .A2(in_2[6]), .A3(in_2[5]), .A4(in_2[4]), .A5(in_2[3]), .DIR(1'b1),
    .A6(in_2[2]), .A7(in_2[1]), .A8(in_2[0]));

  // Notes on the sheet:
  //   SYSTEM BUS
endmodule

module program_counter (
  input  in_1,
  input  in_2,
  input  in_3,
  input  in_4,
  input  in_5,
  input  [7:0] in_6
);

  wire bus0, bus1, bus2, bus3, bus4, bus5, bus6, bus7, n74161_1_pin1, n74161_1_pin9, n74161_1_pin10,
       n74161_1_pin11, n74161_1_pin12, n74161_1_pin13, n74161_1_pin14, not_1_out;

  LED led_1 (.in(bus6));
  LED led_2 (.in(bus5));
  LED led_3 (.in(bus4));
  LED led_4 (.in(bus7));
  not not_1 (not_1_out, in_3);
  LED led_5 (.in(bus3));
  LED led_6 (.in(bus2));
  LED led_7 (.in(bus1));
  LED led_8 (.in(bus0));
  SN74HC245_octal_bus_transceiver_up sn74hc245_octal_bus_transceiver_up_1 (
    .B1(bus7), .B2(bus6), .B3(bus5), .B4(bus4), .B5(bus3), .B6(bus2), .B7(bus1), .B8(bus0),
    .OE_active_low(in_5), .A1(in_6[7]), .A2(in_6[6]), .A3(in_6[5]), .A4(in_6[4]), .A5(in_6[3]), .DIR(1'b1),
    .A6(in_6[2]), .A7(in_6[1]), .A8(in_6[0]));
  SN74HC245_octal_bus_transceiver_down sn74hc245_octal_bus_transceiver_down_1 (
    .A1(bus7), .A2(bus6), .A3(bus5), .A4(bus4), .A5(bus3), .A6(bus2), .A7(bus1), .A8(bus0),
    .OE_active_low(not_1_out), .B1(1'b0), .B2(1'b0), .B3(1'b0), .B4(1'b0), .B5(n74161_1_pin11),
    .B6(n74161_1_pin12), .B7(n74161_1_pin13), .B8(n74161_1_pin14), .DIR(1'b0));
  LED led_9 (.in(n74161_1_pin11));
  LED led_10 (.in(n74161_1_pin12));
  LED led_11 (.in(n74161_1_pin13));
  LED led_12 (.in(n74161_1_pin14));
  _74161 #(.ShowInternalStructure("true")) u_74161_1 (
    .pin1(n74161_1_pin1), .pin2(in_4), .pin3(bus3), .pin4(bus2), .pin5(bus1), .pin6(bus0), .pin7(in_2),
    .pin14(n74161_1_pin14), .pin13(n74161_1_pin13), .pin12(n74161_1_pin12), .pin11(n74161_1_pin11),
    .pin10(n74161_1_pin10), .pin9(n74161_1_pin9));  // open: pin15
  not not_2 (n74161_1_pin9, in_1);
  // also tied to VCC on the sheet: {n74161_1_pin1, n74161_1_pin10}

  // Other names for the same wires on the sheet: clk = in_4; ctrl_PC_en = in_2; ctrl_PC_load = in_1;
  //   ctrl_PC_out = in_3

  // Notes on the sheet:
  //   SYSTEM BUS
  //   PROGRAM COUNTER
endmodule

module register_A (
  input  in_1,
  input  in_2,
  input  in_3,
  input  in_4,
  input  [7:0] in_5
);

  wire a0, a1, a2, a3, a4, a5, a6, a7, bus0, bus1, bus2, bus3, bus4, bus5, bus6, bus7, not_1_out, not_2_out;

  LED led_1 (.in(bus6));
  LED led_2 (.in(bus5));
  LED led_3 (.in(bus4));
  LED led_4 (.in(bus7));
  not not_1 (not_1_out, in_1);
  LED led_5 (.in(bus3));
  LED led_6 (.in(bus2));
  LED led_7 (.in(bus1));
  LED led_8 (.in(bus0));
  SN74HC245_octal_bus_transceiver_up sn74hc245_octal_bus_transceiver_up_1 (
    .B1(bus7), .B2(bus6), .B3(bus5), .B4(bus4), .B5(bus3), .B6(bus2), .B7(bus1), .B8(bus0),
    .OE_active_low(in_4), .A1(in_5[7]), .A2(in_5[6]), .A3(in_5[5]), .A4(in_5[4]), .A5(in_5[3]), .DIR(1'b1),
    .A6(in_5[2]), .A7(in_5[1]), .A8(in_5[0]));
  SN74HC245_octal_bus_transceiver_up sn74hc245_octal_bus_transceiver_up_2 (
    .B1(bus7), .B2(bus6), .B3(bus5), .B4(bus4), .B5(bus3), .B6(bus2), .B7(bus1), .B8(bus0),
    .OE_active_low(not_1_out), .A1(a7), .A2(a6), .A3(a5), .A4(a4), .A5(a3), .DIR(1'b1), .A6(a2), .A7(a1),
    .A8(a0));
  LED led_9 (.in(a7));
  LED led_10 (.in(a6));
  LED led_11 (.in(a5));
  LED led_12 (.in(a4));
  LED led_13 (.in(a3));
  LED led_14 (.in(a2));
  LED led_15 (.in(a1));
  LED led_16 (.in(a0));
  CD74HC173_quad_D_type_flip_flop cd74hc173_quad_d_type_flip_flop_1 (
    .Q0(a7), .Q1(a6), .Q2(a5), .Q3(a4), .E1_active_low(not_2_out), .E2_active_low(not_2_out), .CP(in_3),
    .MR(1'b0), .OE1_active_low(1'b0), .D0(bus7), .D1(bus6), .D2(bus5), .OE2_active_low(1'b0), .D3(bus4));
  not not_2 (not_2_out, in_2);
  CD74HC173_quad_D_type_flip_flop cd74hc173_quad_d_type_flip_flop_2 (
    .Q0(a3), .Q1(a2), .Q2(a1), .Q3(a0), .E1_active_low(not_2_out), .E2_active_low(not_2_out), .CP(in_3),
    .MR(1'b0), .OE1_active_low(1'b0), .D0(bus3), .D1(bus2), .D2(bus1), .OE2_active_low(1'b0), .D3(bus0));

  // Other names for the same wires on the sheet: clk = in_3; ctrl_Ra_in = in_2; ctrl_Ra_out = in_1

  // Notes on the sheet:
  //   REGISTER A
  //   SYSTEM BUS
endmodule

module register_B (
  input  in_1,
  input  in_2,
  input  in_3,
  input  in_4,
  input  [7:0] in_5
);

  wire b0, b1, b2, b3, b4, b5, b6, b7, bus0, bus1, bus2, bus3, bus4, bus5, bus6, bus7, not_1_out, not_2_out;

  LED led_1 (.in(bus6));
  LED led_2 (.in(bus5));
  LED led_3 (.in(bus4));
  LED led_4 (.in(bus7));
  not not_1 (not_1_out, in_1);
  LED led_5 (.in(bus3));
  LED led_6 (.in(bus2));
  LED led_7 (.in(bus1));
  LED led_8 (.in(bus0));
  SN74HC245_octal_bus_transceiver_up sn74hc245_octal_bus_transceiver_up_1 (
    .B1(bus7), .B2(bus6), .B3(bus5), .B4(bus4), .B5(bus3), .B6(bus2), .B7(bus1), .B8(bus0),
    .OE_active_low(in_4), .A1(in_5[7]), .A2(in_5[6]), .A3(in_5[5]), .A4(in_5[4]), .A5(in_5[3]), .DIR(1'b1),
    .A6(in_5[2]), .A7(in_5[1]), .A8(in_5[0]));
  LED led_9 (.in(b7));
  SN74HC245_octal_bus_transceiver_down sn74hc245_octal_bus_transceiver_down_1 (
    .A1(bus7), .A2(bus6), .A3(bus5), .A4(bus4), .A5(bus3), .A6(bus2), .A7(bus1), .A8(bus0),
    .OE_active_low(not_1_out), .B1(b7), .B2(b6), .B3(b5), .B4(b4), .B5(b3), .B6(b2), .B7(b1), .B8(b0),
    .DIR(1'b0));
  LED led_10 (.in(b6));
  LED led_11 (.in(b5));
  LED led_12 (.in(b4));
  LED led_13 (.in(b3));
  LED led_14 (.in(b2));
  LED led_15 (.in(b1));
  LED led_16 (.in(b0));
  CD74HC173_quad_D_type_flip_flop cd74hc173_quad_d_type_flip_flop_1 (
    .Q0(b4), .Q1(b5), .Q2(b6), .Q3(b7), .E1_active_low(not_2_out), .E2_active_low(not_2_out), .CP(in_3),
    .MR(1'b0), .OE1_active_low(1'b0), .D0(bus4), .D1(bus5), .D2(bus6), .OE2_active_low(1'b0), .D3(bus7));
  CD74HC173_quad_D_type_flip_flop cd74hc173_quad_d_type_flip_flop_2 (
    .Q0(b0), .Q1(b1), .Q2(b2), .Q3(b3), .E1_active_low(not_2_out), .E2_active_low(not_2_out), .CP(in_3),
    .MR(1'b0), .OE1_active_low(1'b0), .D0(bus0), .D1(bus1), .D2(bus2), .OE2_active_low(1'b0), .D3(bus3));
  not not_2 (not_2_out, in_2);

  // Other names for the same wires on the sheet: clk = in_3; ctrl_Rb_in = in_2; ctrl_Rb_out = in_1

  // Notes on the sheet:
  //   SYSTEM BUS
  //   REGISTER B
endmodule

module ALU (
  input  in_1,
  input  in_2,
  input  [7:0] in_3,
  input  in_4,
  input  [7:0] in_5,
  input  [7:0] in_6
);

  wire bus0, bus1, bus2, bus3, bus4, bus5, bus6, bus7, n0, n1, n2, n3, n4, n5, n6, n7, n74283_1_pin7,
       n74283_1_pin9, not_1_out, s0, s1, s2, s3, s4, s5, s6, s7;

  LED led_1 (.in(bus7));
  LED led_2 (.in(bus6));
  LED led_3 (.in(bus5));
  not not_1 (not_1_out, in_1);
  LED led_4 (.in(bus4));
  LED led_5 (.in(bus3));
  LED led_6 (.in(bus2));
  LED led_7 (.in(bus1));
  LED led_8 (.in(bus0));
  SN74HC245_octal_bus_transceiver_up sn74hc245_octal_bus_transceiver_up_1 (
    .B1(bus7), .B2(bus6), .B3(bus5), .B4(bus4), .B5(bus3), .B6(bus2), .B7(bus1), .B8(bus0),
    .OE_active_low(in_4), .A1(in_6[7]), .A2(in_6[6]), .A3(in_6[5]), .A4(in_6[4]), .A5(in_6[3]), .DIR(1'b1),
    .A6(in_6[2]), .A7(in_6[1]), .A8(in_6[0]));
  SN74HC245_octal_bus_transceiver_up sn74hc245_octal_bus_transceiver_up_2 (
    .B1(bus7), .B2(bus6), .B3(bus5), .B4(bus4), .B5(bus3), .B6(bus2), .B7(bus1), .B8(bus0),
    .OE_active_low(not_1_out), .A1(s7), .A2(s6), .A3(s5), .A4(s4), .A5(s3), .DIR(1'b1), .A6(s2), .A7(s1),
    .A8(s0));
  LED led_9 (.in(s7));
  LED led_10 (.in(s6));
  LED led_11 (.in(s5));
  LED led_12 (.in(s4));
  LED led_13 (.in(s3));
  LED led_14 (.in(s2));
  LED led_15 (.in(s1));
  LED led_16 (.in(s0));
  _74283 #(.ShowInternalStructure("true")) u_74283_1 (
    .pin1(s5), .pin2(n5), .pin3(in_3[5]), .pin4(s4), .pin5(in_3[4]), .pin6(n4), .pin7(n74283_1_pin7),
    .pin15(n6), .pin14(in_3[6]), .pin13(s6), .pin12(in_3[7]), .pin11(n7), .pin10(s7), .pin9(n74283_1_pin9));
  LED overflow (.in(n74283_1_pin9));
  _7486 #(.ShowInternalStructure("true")) u_7486_1 (
    .pin1(in_2), .pin2(in_5[4]), .pin3(n4), .pin4(in_2), .pin5(in_5[5]), .pin6(n5), .pin13(in_5[7]),
    .pin12(in_2), .pin11(n7), .pin10(in_5[6]), .pin9(in_2), .pin8(n6));
  _74283 #(.ShowInternalStructure("true")) u_74283_2 (
    .pin1(s1), .pin2(n1), .pin3(in_3[1]), .pin4(s0), .pin5(in_3[0]), .pin6(n0), .pin7(in_2), .pin15(n2),
    .pin14(in_3[2]), .pin13(s2), .pin12(in_3[3]), .pin11(n3), .pin10(s3), .pin9(n74283_1_pin7));
  _7486 #(.ShowInternalStructure("true")) u_7486_2 (
    .pin1(in_2), .pin2(in_5[0]), .pin3(n0), .pin4(in_2), .pin5(in_5[1]), .pin6(n1), .pin13(in_5[3]),
    .pin12(in_2), .pin11(n3), .pin10(in_5[2]), .pin9(in_2), .pin8(n2));

  // Other names for the same wires on the sheet: ctrl_ALU_out = in_1; ctrl_ALU_sub = in_2; a0 = in_3[0]; a1 = in_3[1];
  //   a2 = in_3[2]; a3 = in_3[3]; a4 = in_3[4]; a5 = in_3[5]; a6 = in_3[6]; a7 = in_3[7]; b0 = in_5[0]; b1 = in_5[1];
  //   b2 = in_5[2]; b3 = in_5[3]; b4 = in_5[4]; b5 = in_5[5]; b6 = in_5[6]; b7 = in_5[7]

  // Notes on the sheet:
  //   SYSTEM BUS
  //   ALU [a0 .. a7] is register A, [b0 .. b7] is register B, [n0 .. n7] is negated content of register B,  [s0 .. s7] is result
endmodule

module CD74HC173_quad_D_type_flip_flop (
  input  OE1_active_low,
  input  OE2_active_low,
  input  E1_active_low,
  input  E2_active_low,
  input  CP,
  input  MR,
  input  D0,
  input  D1,
  input  D2,
  input  D3,
  output Q0,
  output Q1,
  output Q2,
  output Q3
);

  wire and_1_out, and_2_out, and_3_out, and_4_out, and_5_out, and_6_out, and_7_out, and_8_out, buffer_1_out,
       buffer_2_out, buffer_3_out, buffer_4_out, buffer_7_out, buffer_8_out, buffer_9_out, buffer_10_out,
       CP_t, d_ff_1_q, d_ff_2_q, d_ff_3_q, d_ff_4_q, E, MR_t, not_E, OE, or_2_out, or_3_out, or_4_out,
       or_5_out;

  buf buffer_1 (buffer_1_out, OE1_active_low);
  buf buffer_2 (buffer_2_out, OE2_active_low);
  buf buffer_3 (buffer_3_out, E1_active_low);
  buf buffer_4 (buffer_4_out, E2_active_low);
  buf buffer_5 (CP_t, CP);
  buf buffer_6 (MR_t, MR);
  buf buffer_7 (buffer_7_out, D0);
  buf buffer_8 (buffer_8_out, D1);
  buf buffer_9 (buffer_9_out, D2);
  buf buffer_10 (buffer_10_out, D3);
  nor nor_1 (OE, buffer_1_out, buffer_2_out);
  or or_1 (E, buffer_3_out, buffer_4_out);
  not not_1 (not_E, E);
  and and_1 (and_1_out, d_ff_1_q, E);
  and and_2 (and_2_out, not_E, buffer_7_out);
  and and_3 (and_3_out, d_ff_2_q, E);
  and and_4 (and_4_out, not_E, buffer_8_out);
  and and_5 (and_5_out, d_ff_3_q, E);
  and and_6 (and_6_out, not_E, buffer_9_out);
  and and_7 (and_7_out, d_ff_4_q, E);
  and and_8 (and_8_out, not_E, buffer_10_out);
  D_Flip_Flop d_ff_1 (.D(or_2_out), .clk(CP_t), .Q(d_ff_1_q), .reset(MR_t));  // open: Qn, preset
  or or_2 (or_2_out, and_1_out, and_2_out);
  D_Flip_Flop d_ff_2 (.D(or_3_out), .clk(CP_t), .Q(d_ff_2_q), .reset(MR_t));  // open: Qn, preset
  or or_3 (or_3_out, and_3_out, and_4_out);
  D_Flip_Flop d_ff_3 (.D(or_4_out), .clk(CP_t), .Q(d_ff_3_q), .reset(MR_t));  // open: Qn, preset
  or or_4 (or_4_out, and_5_out, and_6_out);
  D_Flip_Flop d_ff_4 (.D(or_5_out), .clk(CP_t), .Q(d_ff_4_q), .reset(MR_t));  // open: Qn, preset
  or or_5 (or_5_out, and_7_out, and_8_out);
  assign Q0 = OE ? d_ff_1_q : 1'bz;  // Controlled_Buffer controlled_buffer_1
  assign Q1 = OE ? d_ff_2_q : 1'bz;  // Controlled_Buffer controlled_buffer_2
  assign Q2 = OE ? d_ff_3_q : 1'bz;  // Controlled_Buffer controlled_buffer_3
  assign Q3 = OE ? d_ff_4_q : 1'bz;  // Controlled_Buffer controlled_buffer_4
endmodule

module SN74HC245_octal_bus_transceiver_up (
  input  DIR,
  input  OE_active_low,
  input  A1,
  input  A2,
  input  A3,
  input  A4,
  input  A5,
  input  A6,
  input  A7,
  input  A8,
  output B1,
  output B2,
  output B3,
  output B4,
  output B5,
  output B6,
  output B7,
  output B8
);

  wire and_1_out, and_2_out;

  and and_1 (and_1_out, DIR, ~OE_active_low);  // AND_Gate
  assign B1 = and_1_out ? A1 : 1'bz;  // Controlled_Buffer controlled_buffer_1
  assign B2 = and_1_out ? A2 : 1'bz;  // Controlled_Buffer controlled_buffer_2
  assign B3 = and_1_out ? A3 : 1'bz;  // Controlled_Buffer controlled_buffer_3
  assign B4 = and_1_out ? A4 : 1'bz;  // Controlled_Buffer controlled_buffer_4
  assign B5 = and_1_out ? A5 : 1'bz;  // Controlled_Buffer controlled_buffer_5
  assign B6 = and_1_out ? A6 : 1'bz;  // Controlled_Buffer controlled_buffer_6
  assign B7 = and_1_out ? A7 : 1'bz;  // Controlled_Buffer controlled_buffer_7
  assign B8 = and_1_out ? A8 : 1'bz;  // Controlled_Buffer controlled_buffer_8
  and and_2 (and_2_out, ~DIR, ~OE_active_low);  // AND_Gate
  assign A1 = and_2_out ? B1 : 1'bz;  // Controlled_Buffer controlled_buffer_9
  assign A2 = and_2_out ? B2 : 1'bz;  // Controlled_Buffer controlled_buffer_10
  assign A3 = and_2_out ? B3 : 1'bz;  // Controlled_Buffer controlled_buffer_11
  assign A4 = and_2_out ? B4 : 1'bz;  // Controlled_Buffer controlled_buffer_12
  assign A5 = and_2_out ? B5 : 1'bz;  // Controlled_Buffer controlled_buffer_13
  assign A6 = and_2_out ? B6 : 1'bz;  // Controlled_Buffer controlled_buffer_14
  assign A7 = and_2_out ? B7 : 1'bz;  // Controlled_Buffer controlled_buffer_15
  assign A8 = and_2_out ? B8 : 1'bz;  // Controlled_Buffer controlled_buffer_16
endmodule

module SN74HC245_octal_bus_transceiver_down (
  input  DIR,
  input  OE_active_low,
  input  B1,
  input  B2,
  input  B3,
  input  B4,
  input  B5,
  input  B6,
  input  B7,
  input  B8,
  output A1,
  output A2,
  output A3,
  output A4,
  output A5,
  output A6,
  output A7,
  output A8
);

  wire and_1_out, and_2_out;

  and and_1 (and_1_out, DIR, ~OE_active_low);  // AND_Gate
  assign B1 = and_1_out ? A1 : 1'bz;  // Controlled_Buffer controlled_buffer_1
  assign B2 = and_1_out ? A2 : 1'bz;  // Controlled_Buffer controlled_buffer_2
  assign B3 = and_1_out ? A3 : 1'bz;  // Controlled_Buffer controlled_buffer_3
  assign B4 = and_1_out ? A4 : 1'bz;  // Controlled_Buffer controlled_buffer_4
  assign B5 = and_1_out ? A5 : 1'bz;  // Controlled_Buffer controlled_buffer_5
  assign B6 = and_1_out ? A6 : 1'bz;  // Controlled_Buffer controlled_buffer_6
  assign B7 = and_1_out ? A7 : 1'bz;  // Controlled_Buffer controlled_buffer_7
  assign B8 = and_1_out ? A8 : 1'bz;  // Controlled_Buffer controlled_buffer_8
  and and_2 (and_2_out, ~DIR, ~OE_active_low);  // AND_Gate
  assign A1 = and_2_out ? B1 : 1'bz;  // Controlled_Buffer controlled_buffer_9
  assign A2 = and_2_out ? B2 : 1'bz;  // Controlled_Buffer controlled_buffer_10
  assign A3 = and_2_out ? B3 : 1'bz;  // Controlled_Buffer controlled_buffer_11
  assign A4 = and_2_out ? B4 : 1'bz;  // Controlled_Buffer controlled_buffer_12
  assign A5 = and_2_out ? B5 : 1'bz;  // Controlled_Buffer controlled_buffer_13
  assign A6 = and_2_out ? B6 : 1'bz;  // Controlled_Buffer controlled_buffer_14
  assign A7 = and_2_out ? B7 : 1'bz;  // Controlled_Buffer controlled_buffer_15
  assign A8 = and_2_out ? B8 : 1'bz;  // Controlled_Buffer controlled_buffer_16
endmodule
